# Fritzing sketch final_breadboard (saved by Fritzing 0.9.3b)
breadboards: 1

parts:
  R1 = BBC MicroBit  # not connected
  Part1 = Adafruit DragonTail for micro:bit [part_number=3695]
  74AHCT125 = IC, DIP package, 14 pins [chip_label=74AHCT125]
  Part2 = Digital FM Radio Receiver
  C1 = Electrolytic Capacitor [capacitance=1000μF voltage=16V package="1010 [SMD, electrolytic]"]  # not connected

nets:
  N1: Part1.SDA, Part2.SDIO
  N2: Part1.SCL, Part2.SCLK
  N3: Part1.P16, Part2.!RST
  N4: Part1.P15, 74AHCT125.pin2
  N5: Part1.P13, 74AHCT125.pin5
  N6: Part1.GND, 74AHCT125.pin9, 74AHCT125.pin12, 74AHCT125.pin13
  N7: 74AHCT125.pin1, 74AHCT125.pin4, 74AHCT125.pin7, Part2.GND

notes:
  Ground
  +3.3V DC
  +5V DC
  APA-102 LED Strip
  +5V
  GND
  DATA
  CLK
  Amplifier + Speakers
  Microbit controlling FM receiver and Apa102 LED strip
  The Public Radio

custom parts:
  BBC MicroBit: The BBC MICRO:BIT
  Adafruit DragonTail for micro:bit: This breakout board has the card-edge connector for your micro:bit, and then breaks out all the pads so that it can be plugged in to any solderless breadboard. You even get two pads for the power railing! It comes fully assembled - no soldering required. And every pad is clearly labeled: by name, if it has an analog input, and when it is shared with the LED matrix.
